// Logisim project AND.circ as structural Verilog: 1 circuit, main circuit main
module main (
  input  A,
  input  B,
  output out_3
);

  and and_1 (out_3, A, A, B);

  // Notes on the sheet:
  //   A
  //   0
  //   0
  //   1
  //   1
  //   B
  //   0
  //   1
  //   0
  //   1
  //   X
  //   0
  //   0
  //   0
  //   1
endmodule
