// Logisim project BUFFER GATE.circ as structural Verilog: 1 circuit, main circuit main
module main (
  input  in_1,
  input  in_2
);

  wire BUFFER_2_out, BUFFER_out;

  buf BUFFER (BUFFER_out, in_1);
  buf BUFFER_2 (BUFFER_2_out, in_2);
  LED led_1 (.in(BUFFER_out));
  LED led_2 (.in(BUFFER_2_out));

  // Notes on the sheet:
  //   BUFFER GATE
  //   TRUTH TABLE
  //   A              Y
  //   0               0
  //   1                1
endmodule
