// Logisim project D flip flop.circ as structural Verilog: 1 circuit, main circuit main
module main (
  input  D,
  input  in_2,
  output Q,
  output Q_prime,
  output out_5,
  output out_6
);

  wire AND_2_out, AND_out, clock_1_out, clock_2_out, NOT_out;

  not NOT (NOT_out, D);
  Clock clock_1 (.out(clock_1_out));
  Clock clock_2 (.out(clock_2_out));
  D_Flip_Flop d_ff_1 (.clk(in_2), .D(clock_1_out), .Q(out_5), .Qn(out_6));  // open: preset, en, reset
  and AND (AND_out, D, clock_2_out);
  and AND_2 (AND_2_out, clock_2_out, NOT_out);
  nor NOR (Q, AND_out, Q_prime);
  nor NOR_2 (Q_prime, Q, AND_2_out);

  // Notes on the sheet:
  //   clk
  //   Block Diagram of D flip flop
  //   Circuit diagram of D flip flop
  //   E
  //   0
  //   0
  //   1
  //   1
  //   D
  //   Q
  //   Q
  //   0
  //   1
  //   Q
  //   0
  //   0
  //   1
  //   1
  //   Truth Table of D Flip Flop
  //   Q'
  //   Q'
  //   Q'
  //   1
  //   0
  //   E=Enable
  //   D=Input
  //   Q=Output
  //   Q'= Output
endmodule
