// Logisim project NAND.circ as structural Verilog: 1 circuit, main circuit main
module main (
  input  in_1,
  input  in_2,
  output out_3
);

  wire and_1_out;

  and and_1 (and_1_out, in_1, in_2);
  not not_1 (out_3, and_1_out);

  // Notes on the sheet:
  //   A
  //   0
  //   0
  //   1
  //   1
  //   B
  //   0
  //   1
  //   0
  //   1
  //   X
  //   1
  //   1
  //   1
  //   0
endmodule
