// Logisim project ORGATE.circ as structural Verilog: 1 circuit, main circuit main
module main (
  input  in_1,
  input  in_2,
  output out_3
);

  or or_1 (out_3, in_1, in_2);

  // Notes on the sheet:
  //   A
  //   0
  //   0
  //   1
  //   1
  //   B
  //   0
  //   1
  //   0
  //   1
  //   X
  //   0
  //   1
  //   1
  //   1
endmodule
