// Logisim project SR flipflop.circ as structural Verilog: 1 circuit, main circuit main
module main (
  input  in_1,
  input  in_2,
  input  in_3,
  input  in_4
);

  wire clock_1_out, nand_1_out, nand_2_out, SR_FLIP_FLOP_q, SR_FLIP_FLOP_qn;

  Clock clock_1 (.out(clock_1_out));
  S_R_Flip_Flop SR_FLIP_FLOP (
    .S(SR_FLIP_FLOP_qn), .R(SR_FLIP_FLOP_q), .Q(SR_FLIP_FLOP_q), .Qn(SR_FLIP_FLOP_qn), .preset(in_1),
    .reset(in_2), .en(clock_1_out));  // open: clk
  LED led_1 (.in(SR_FLIP_FLOP_q));
  LED led_2 (.in(SR_FLIP_FLOP_qn));
  nand nand_1 (nand_1_out, in_3, nand_2_out);
  nand nand_2 (nand_2_out, nand_1_out, in_4);
  LED led_3 (.in(nand_1_out));
  LED led_4 (.in(nand_2_out));

  // Notes on the sheet:
  //   S(SET)
  //   R(RESET)
  //                                TRUTH TABLE
  //   S
  //   0
  //   0
  //   1
  //   1
  //   R
  //   Q
  //   1
  //   0
  //   1
  //   1
  //   0
  //   0
  //   1
  //   1
  //   Q'
  //   1
  //     0                            
  //   1
  //   0
  //   Q
  //   Q'
endmodule
