// Logisim project T flipflop.circ as structural Verilog: 1 circuit, main circuit main
module main (
  input  T
);

  wire and_1_out, and_2_out, clock_1_out, nor_1_out, nor_2_out, T_FLIP_FLOP_q, T_FLIP_FLOP_qn, undriven,
       undriven_2;

  Clock clock_1 (.out(clock_1_out));
  T_Flip_Flop T_FLIP_FLOP (
    .clk(undriven), .T(undriven_2), .Q(T_FLIP_FLOP_q), .Qn(T_FLIP_FLOP_qn));  // open: preset, reset, en
  and and_1 (and_1_out, nor_1_out, T, clock_1_out);
  and and_2 (and_2_out, clock_1_out, T, nor_2_out);
  nor nor_1 (nor_1_out, and_1_out, nor_2_out);
  nor nor_2 (nor_2_out, nor_1_out, and_2_out);
  LED led_1 (.in(nor_1_out));
  LED led_2 (.in(nor_2_out));

  // Notes on the sheet:
  //   Q
  //   T
  //            Q(t+1)
  //   0
  //   0
  //   0
  //   1
  //   1
  //   0
  //   0
  //   1
  //   0
  //   1
  //   1
  //   0
  //   Q
  //   Q'
endmodule
