// Logisim project XOR.circ as structural Verilog: 1 circuit, main circuit main
module main (
  input  in_1,
  input  in_2,
  input  in_3,
  input  in_4,
  output out_5
);

  wire and_1_out, and_2_out, not_1_out, not_2_out;

  not not_1 (not_1_out, in_2);
  not not_2 (not_2_out, in_4);
  and and_1 (and_1_out, in_1, not_1_out);
  and and_2 (and_2_out, in_3, not_2_out);
  or or_1 (out_5, and_1_out, and_2_out);

  // Notes on the sheet:
  //   A
  //   0
  //   0
  //   0
  //   0
  //   1
  //   1
  //   1
  //   1
  //   B
  //   0
  //   0
  //   1
  //   1
  //   0
  //   0
  //   1
  //   1
  //   c
  //   0
  //   1
  //   0
  //   1
  //   0
  //   1
  //   0
  //   1
  //   X
  //   0
  //   1
  //   1
  //   0
  //   1
  //   0
  //   0
  //   1
endmodule
